// Logisim project alu.circ as structural Verilog: 1 circuit, main circuit main
module main (
  input  X2X1X0,
  input  [1:0] in_2,
  input  [3:0] A,
  input  [3:0] B,
  output [3:0] out_5,
  output out_6,
  output out_7
);

  wire and_2_out, and_3_out, not_1_out, not_2_out, not_3_out;
  wire [3:0] adder_1_out, and_1_out, or_1_out, xor_1_out;
  wire [3:3] comparator_1_lt;

  assign and_1_out = A & B;  // AND_Gate and_1, 4 bits wide
  assign or_1_out = A | B;  // OR_Gate or_1, 4 bits wide
  not not_1 (not_1_out, A[3]);
  Multiplexer #(.select(2), .width(4), .enable("false")) multiplexer_1 (
    .in0(and_1_out), .in1(or_1_out), .in2(adder_1_out), .in3({4{comparator_1_lt[3]}}), .out(out_5), .sel(in_2));
  nor nor_1 (out_6, out_5[3], out_5[2], out_5[1], out_5[0]);
  not not_2 (not_2_out, B[3]);
  and and_2 (and_2_out, not_1_out, not_2_out, adder_1_out[3]);
  or or_2 (out_7, and_2_out, and_3_out);
  xor xor_1 (xor_1_out[0], B[0], X2X1X0);
  xor xor_2 (xor_1_out[1], B[1], X2X1X0);
  xor xor_3 (xor_1_out[2], B[2], X2X1X0);
  xor xor_4 (xor_1_out[3], B[3], X2X1X0);
  not not_3 (not_3_out, adder_1_out[3]);
  and and_3 (and_3_out, B[3], A[3], not_3_out);
  Adder #(.width(4)) adder_1 (.a(xor_1_out), .b(A), .out(adder_1_out), .cin(X2X1X0));  // open: cout
  Comparator #(.width(4), .mode("unsigned")) comparator_1 (.a(A), .b(B), .lt(comparator_1_lt[3]));  // open: gt, eq

  // Notes on the sheet:
  //   X2X1X0
  //   000 AND -> A & B
  //   001 OR -> A OR B
  //   010 SUMA -> A + B
  //   110 RESTA -> A - B
  //   111 SLT -> IF(A < B) RETURN 1
  //   Salida Zero Overflow
endmodule
