// Logisim project contador_registro.circ as structural Verilog: 1 circuit, main circuit main
module main (
  input  Load,
  input  Count_Enable,
  input  [3:0] Input,
  input  Mem_Enable,
  output [3:0] Count_Output,
  output [3:0] Mem_Output
);

  wire and_1_out, clock_1_out, not_1_out;

  Clock clock_1 (.out(clock_1_out));
  not not_1 (not_1_out, Load);
  and and_1 (and_1_out, not_1_out, Count_Enable);
  Counter #(.width(4), .max('hf)) counter_1 (
    .load(Load), .D(Input), .count(and_1_out), .Q(Count_Output), .clk(clock_1_out), .clr(1'b0));  // open: carry
  Register #(.width(4)) register_1 (.D(Input), .en(Mem_Enable), .Q(Mem_Output), .clk(clock_1_out), .clr(1'b0));

  // Notes on the sheet:
  //   Clock
endmodule
