// Logisim project conversor serie-paralelo.circ as structural Verilog: 1 circuit, main circuit main
module main (
  input  Bit,
  input  Write,
  input  Read,
  input  [7:0] Code,
  output Ready,
  output Memoria,
  output out_7,
  output out_8,
  output out_9,
  output out_10,
  output out_11,
  output Data,
  output out_13,
  output out_14
);

  wire and_1_out, and_2_out, and_3_out, and_4_out, and_5_out, and_6_out, and_7_out, and_8_out, and_9_out,
       and_10_out, and_12_out, clock_1_out, counter_1_q, nand_1_out, not_1_out, not_3_out, not_4_out,
       not_5_out, not_6_out, not_7_out, not_8_out, not_9_out, not_10_out, not_11_out, not_12_out, not_13_out,
       not_14_out, not_15_out, not_16_out, or_1_out, xnor_1_out;
  wire [1:0] and_11_out, multiplexer_2_out;
  wire [1:1] not_18_out;
  wire [3:0] adder_1_out, counter_2_q;
  wire [7:0] demultiplexer_1_out0;
  wire [9:5] d_ff_5_q;

  Clock clock_1 (.out(clock_1_out));
  Counter #(.width(1), .max('h1)) counter_1 (
    .Q(counter_1_q), .clk(and_1_out), .clr(d_ff_5_q[5]));  // open: load, D, count, carry
  not not_1 (not_1_out, Write);
  xnor xnor_1 (xnor_1_out, not_1_out, Ready);
  Counter #(.width(4), .max('hf)) counter_2 (
    .Q(counter_2_q), .clk(clock_1_out), .clr(or_1_out));  // open: load, D, count, carry
  or or_1 (or_1_out, xnor_1_out, and_1_out);
  and and_1 (and_1_out, counter_2_q[3], counter_2_q[0]);
  Demultiplexer #(.select(3)) demultiplexer_1 (
    .out0(demultiplexer_1_out0[0]), .out1(demultiplexer_1_out0[1]), .out2(demultiplexer_1_out0[2]),
    .out3(demultiplexer_1_out0[3]), .out4(demultiplexer_1_out0[4]), .out5(demultiplexer_1_out0[5]),
    .out6(demultiplexer_1_out0[6]), .out7(demultiplexer_1_out0[7]), .in(Bit), .sel(counter_2_q[2:0]),
    .en(Ready));
  not not_2 (Ready, counter_1_q);
  and and_2 (and_2_out, counter_2_q[0], clock_1_out, not_3_out, not_4_out);
  not not_3 (not_3_out, counter_2_q[1]);
  not not_4 (not_4_out, counter_2_q[2]);
  not not_5 (not_5_out, counter_2_q[2]);
  and and_3 (and_3_out, not_5_out, counter_2_q[1], clock_1_out, not_6_out);
  not not_6 (not_6_out, counter_2_q[0]);
  not not_7 (not_7_out, counter_2_q[2]);
  and and_4 (and_4_out, not_7_out, counter_2_q[1], counter_2_q[0], clock_1_out);
  not not_8 (not_8_out, counter_2_q[0]);
  and and_5 (and_5_out, not_8_out, clock_1_out, counter_2_q[2], not_9_out);
  not not_9 (not_9_out, counter_2_q[1]);
  and and_6 (and_6_out, clock_1_out, counter_2_q[0], counter_2_q[2], not_10_out);
  not not_10 (not_10_out, counter_2_q[1]);
  and and_7 (and_7_out, clock_1_out, counter_2_q[1], counter_2_q[2], not_11_out);
  not not_11 (not_11_out, counter_2_q[0]);
  and and_8 (and_8_out, clock_1_out, counter_2_q[0], counter_2_q[1], counter_2_q[2]);
  and and_9 (and_9_out, clock_1_out, not_12_out, counter_2_q[3]);
  not not_12 (not_12_out, counter_2_q[0]);
  D_Flip_Flop #(.trigger("high")) d_ff_1 (
    .clk(clock_1_out), .D(demultiplexer_1_out0[1]), .Q(out_9), .en(and_2_out), .reset(1'b0));  // open: Qn, preset
  D_Flip_Flop #(.trigger("high")) d_ff_2 (
    .clk(clock_1_out), .D(demultiplexer_1_out0[2]), .Q(out_8), .en(and_3_out), .reset(1'b0));  // open: Qn, preset
  D_Flip_Flop #(.trigger("high")) d_ff_3 (
    .clk(clock_1_out), .D(demultiplexer_1_out0[3]), .Q(out_7), .en(and_4_out), .reset(1'b0));  // open: Qn, preset
  D_Flip_Flop #(.trigger("high")) d_ff_4 (
    .clk(clock_1_out), .D(demultiplexer_1_out0[4]), .Q(Memoria), .en(and_5_out), .reset(1'b0));  // open: Qn, preset
  D_Flip_Flop #(.trigger("high")) d_ff_5 (
    .clk(clock_1_out), .D(demultiplexer_1_out0[5]), .Q(d_ff_5_q[6]), .en(and_6_out), .reset(1'b0));  // open: Qn, preset
  D_Flip_Flop #(.trigger("high")) d_ff_6 (
    .clk(clock_1_out), .D(demultiplexer_1_out0[6]), .Q(d_ff_5_q[7]), .en(and_7_out), .reset(1'b0));  // open: Qn, preset
  D_Flip_Flop #(.trigger("high")) d_ff_7 (
    .clk(clock_1_out), .D(demultiplexer_1_out0[7]), .Q(d_ff_5_q[8]), .en(and_8_out), .reset(1'b0));  // open: Qn, preset
  D_Flip_Flop #(.trigger("high")) d_ff_8 (
    .clk(clock_1_out), .D(demultiplexer_1_out0[0]), .Q(d_ff_5_q[9]), .en(and_9_out), .reset(1'b0));  // open: Qn, preset
  not not_13 (not_13_out, Code[3]);
  and and_10 (and_10_out, Code[7], Code[6], Code[5], Code[4], not_13_out, not_14_out, not_15_out);
  Adder #(.width(4)) adder_1 (
    .a({Memoria, out_7, out_8, out_9}), .b(d_ff_5_q[9:6]), .out(adder_1_out), .cout(out_10));  // open: cin
  not not_14 (not_14_out, Code[2]);
  not not_15 (not_15_out, Code[1]);
  nand nand_1 (nand_1_out, Ready, and_12_out);
  not not_16 (not_16_out, Code[0]);
  and and_11 (and_11_out[0], nand_1_out, and_12_out);
  and and_12 (and_12_out, Read, not_16_out, and_10_out);
  and and_13 (d_ff_5_q[5], Read, Code[0], and_10_out);
  Multiplexer #(.select(2), .width(4)) multiplexer_1 (
    .in0(adder_1_out), .in1(4'b0001), .in2(4'b0000), .in3(4'b0000), .out({out_11, Data, out_13, out_14}),
    .sel(multiplexer_2_out), .en(1'b1));
  Multiplexer #(.width(2)) multiplexer_2 (
    .in0(and_11_out), .in1({2{not_18_out[1]}}), .out(multiplexer_2_out), .sel(d_ff_5_q[5]), .en(1'b1));
  not not_17 (and_11_out[1], and_11_out[0]);
  not not_18 (not_18_out[1], d_ff_5_q[5]);

  // Notes on the sheet:
  //   CLK
  //   Serie
  //   Paralelo
  //   0001
  //   Nº Almacenado
endmodule
