// Logisim project multiplicador 3 bits.circ as structural Verilog: 1 circuit, main circuit main
module main (
  input  [2:0] B,
  input  [2:0] A,
  output [6:0] OUT
);

  wire [3:0] adder_1_cout, and_1_out, and_2_out, and_3_out;

  assign and_1_out = {2'b00, B[2:1]} & {4{A[0]}};  // AND_Gate and_1, 4 bits wide
  Adder #(.width(4)) adder_1 (
    .a(and_1_out), .b(and_2_out), .out({adder_1_cout[2:0], OUT[1]}), .cin(1'b0), .cout(adder_1_cout[3]));
  assign and_2_out = {1'b0, B} & {4{A[1]}};  // AND_Gate and_2, 4 bits wide
  Adder #(.width(4)) adder_2 (.a(adder_1_cout), .b(and_3_out), .out(OUT[5:2]), .cin(1'b0), .cout(OUT[6]));
  assign and_3_out = {1'b0, B} & {4{A[2]}};  // AND_Gate and_3, 4 bits wide
  and and_4 (OUT[0], B[0], A[0]);
endmodule
