// Logisim project sumador_restador 4 bits.circ as structural Verilog: 1 circuit, main circuit main
module main (
  input  in_1,
  input  S_R,
  input  A,
  input  in_4,
  input  in_5,
  input  B,
  input  in_7,
  input  in_8,
  input  in_9,
  input  in_10,
  input  [3:0] A_2,
  input  [3:0] B_2,
  output out_13,
  output out_14,
  output out_15,
  output out_16,
  output Overflow,
  output [3:0] Salida,
  output Overflow_2
);

  wire adder_1_cout, adder_2_cout, adder_3_cout, and_1_out, and_2_out, and_3_out, and_4_out, not_1_out,
       not_2_out, not_3_out, not_4_out, not_5_out, not_6_out, xor_1_out, xor_2_out, xor_3_out, xor_4_out;
  wire [3:0] xor_5_out;

  xor xor_1 (xor_1_out, in_1, in_8);
  xor xor_2 (xor_2_out, in_1, in_7);
  xor xor_3 (xor_3_out, in_1, B);
  xor xor_4 (xor_4_out, in_1, in_9);
  not not_1 (not_1_out, in_9);
  not not_2 (not_2_out, A);
  Adder #(.width(1)) adder_1 (.a(S_R), .b(xor_1_out), .out(out_16), .cin(in_1), .cout(adder_1_cout));
  Adder #(.width(1)) adder_2 (.a(in_5), .b(xor_2_out), .out(out_15), .cin(adder_1_cout), .cout(adder_2_cout));
  Adder #(.width(1)) adder_3 (.a(in_4), .b(xor_3_out), .out(out_14), .cin(adder_2_cout), .cout(adder_3_cout));
  Adder #(.width(1)) adder_4 (.a(A), .b(xor_4_out), .out(out_13), .cin(adder_3_cout));  // open: cout
  not not_3 (not_3_out, out_13);
  assign xor_5_out = {4{in_10}} ^ B_2;  // XOR_Gate xor_5, 4 bits wide
  and and_1 (and_1_out, out_13, not_2_out, not_1_out);
  or or_1 (Overflow, and_1_out, and_2_out);
  and and_2 (and_2_out, not_3_out, A, in_9);
  not not_4 (not_4_out, A_2[3]);
  not not_5 (not_5_out, B_2[3]);
  not not_6 (not_6_out, Salida[3]);
  Adder #(.width(4)) adder_5 (.a(A_2), .b(xor_5_out), .out(Salida), .cin(in_10));  // open: cout
  and and_3 (and_3_out, Salida[3], not_4_out, not_5_out);
  and and_4 (and_4_out, not_6_out, A_2[3], B_2[3]);
  // Probe on Salida
  or or_2 (Overflow_2, and_3_out, and_4_out);

  // Notes on the sheet:
  //   in_10: pull=down
  //   S/R
  //   Salida
endmodule
